// Logisim project toyCPU.circ as structural Verilog: 8 circuits, main circuit CPU
module CPU (
  input  [3:0] in_1
);

  CPU_DECODER_4x16 cpu_decoder_4x16_1 (.I(in_1));  // open: out_13, out_14, out_15, out_16, out_17, out_2, out_3, out_4, out_5, out_6, out_7, out_8, out_9, out_10, out_11, out_12
endmodule

module CPU_MEM_1_BIT (
  input  I,
  input  S,
  output Q
);

  wire nand_1_out, nand_2_out, nand_4_out;

  nand nand_1 (nand_1_out, I, S);
  nand nand_2 (nand_2_out, nand_1_out, S);
  nand nand_3 (Q, nand_1_out, nand_4_out);
  nand nand_4 (nand_4_out, Q, nand_2_out);
endmodule

module CPU_MEM_8_BIT (
  input  [7:0] I,
  input  S,
  output [7:0] O
);

  CPU_MEM_1_BIT cpu_mem_1_bit_1 (.I(I[0]), .S(S), .Q(O[0]));
  CPU_MEM_1_BIT cpu_mem_1_bit_2 (.I(I[1]), .S(S), .Q(O[1]));
  CPU_MEM_1_BIT cpu_mem_1_bit_3 (.I(I[2]), .S(S), .Q(O[2]));
  CPU_MEM_1_BIT cpu_mem_1_bit_4 (.I(I[3]), .S(S), .Q(O[3]));
  CPU_MEM_1_BIT cpu_mem_1_bit_5 (.I(I[4]), .S(S), .Q(O[4]));
  CPU_MEM_1_BIT cpu_mem_1_bit_6 (.I(I[5]), .S(S), .Q(O[5]));
  CPU_MEM_1_BIT cpu_mem_1_bit_7 (.I(I[6]), .S(S), .Q(O[6]));
  CPU_MEM_1_BIT cpu_mem_1_bit_8 (.I(I[7]), .S(S), .Q(O[7]));
endmodule

module CPU_ENABLER (
  input  [7:0] I,
  input  E,
  output [7:0] O
);

  and and_1 (O[0], I[0], E);
  and and_2 (O[1], I[1], E);
  and and_3 (O[2], I[2], E);
  and and_4 (O[3], I[3], E);
  and and_5 (O[4], I[4], E);
  and and_6 (O[5], I[5], E);
  and and_7 (O[6], I[6], E);
  and and_8 (O[7], I[7], E);
endmodule

module CPU_REG_8_BIT (
  input  [7:0] I,
  input  S,
  input  E,
  output [7:0] O
);

  wire [7:0] cpu_mem_8_bit_1_o;

  CPU_MEM_8_BIT cpu_mem_8_bit_1 (.I(I), .S(S), .O(cpu_mem_8_bit_1_o));
  CPU_ENABLER cpu_enabler_1 (.I(cpu_mem_8_bit_1_o), .E(E), .O(O));
endmodule

module CPU_DECODER_2x4 (
  input  [1:0] AB,
  output out_2,
  output out_3,
  output out_4,
  output out_5
);

  wire not_1_out, not_2_out;

  not not_1 (not_1_out, AB[1]);
  not not_2 (not_2_out, AB[0]);
  and FF (out_2, not_1_out, not_2_out);
  and FT (out_3, not_1_out, AB[0]);
  and TF (out_4, AB[1], not_2_out);
  and TT (out_5, AB[1], AB[0]);

  // Notes on the sheet:
  //   A
  //   !A
  //   B
  //   !B
endmodule

module CPU_DECODER_3x8 (
  input  [2:0] I,
  output out_2,
  output out_3,
  output out_4,
  output out_5,
  output out_6,
  output out_7,
  output out_8,
  output out_9
);

  wire not_1_out, not_2_out, not_3_out;

  not not_1 (not_1_out, I[2]);
  not not_2 (not_2_out, I[1]);
  not not_3 (not_3_out, I[0]);
  and FFF (out_2, not_1_out, not_2_out, not_3_out);
  and FFT (out_3, not_1_out, not_2_out, I[0]);
  and FTF (out_4, not_1_out, I[1], not_3_out);
  and FTT (out_5, not_1_out, I[1], I[0]);
  and TFF (out_6, I[2], not_2_out, not_3_out);
  and TFT (out_7, I[2], not_2_out, I[0]);
  and TTF (out_8, I[2], I[1], not_3_out);
  and TTT (out_9, I[2], I[1], I[0]);

  // Notes on the sheet:
  //   A
  //   B
  //   C
  //   !A
  //   !B
  //   !C
endmodule

module CPU_DECODER_4x16 (
  input  [3:0] I,
  output out_2,
  output out_3,
  output out_4,
  output out_5,
  output out_6,
  output out_7,
  output out_8,
  output out_9,
  output out_10,
  output out_11,
  output out_12,
  output out_13,
  output out_14,
  output out_15,
  output out_16,
  output out_17
);

  wire not_1_out, not_2_out, not_3_out, not_4_out;

  not not_1 (not_1_out, I[3]);
  not not_2 (not_2_out, I[2]);
  not not_3 (not_3_out, I[1]);
  not not_4 (not_4_out, I[0]);
  and FFFF (out_2, not_1_out, not_2_out, not_3_out, not_4_out);
  and FFFT (out_3, not_1_out, not_2_out, not_3_out, I[0]);
  and FFTF (out_4, not_1_out, not_2_out, I[1], not_4_out);
  and FFTT (out_5, not_1_out, not_2_out, I[1], I[0]);
  and FTFF (out_6, not_1_out, I[2], not_3_out, not_4_out);
  and FTFT (out_7, not_1_out, I[2], not_3_out, I[0]);
  and FTTF (out_8, not_1_out, I[2], I[1], not_4_out);
  and FTTT (out_9, not_1_out, I[2], I[1], I[0]);
  and TFFF (out_10, I[3], not_2_out, not_3_out, not_4_out);
  and TFFT (out_11, I[3], not_2_out, not_3_out, I[0]);
  and TFTF (out_12, I[3], not_2_out, I[1], not_4_out);
  and TFTT (out_13, I[3], not_2_out, I[1], I[0]);
  and TTFF (out_14, I[3], I[2], not_3_out, not_4_out);
  and TTFT (out_15, I[3], I[2], not_3_out, I[0]);
  and TTTF (out_16, I[3], I[2], I[1], not_4_out);
  and TTTT (out_17, I[3], I[2], I[1], I[0]);

  // Notes on the sheet:
  //   A
  //   B
  //   C
  //   D
  //   !A
  //   !B
  //   !C
  //   !D
endmodule
